# Fritzing sketch Server (saved by Fritzing 0.9.3b)

parts:
  Raspberry_Pi1 = Raspberry Pi B+
  U1 = LCD-16X2 [package=lcd-16x2_noholes]  # not connected
  LED1 = smd LED [color="Red (633nm)" package="1206 [SMD]"]
  LED2 = smd LED [color="Red (633nm)" package="1206 [SMD]"]
  IR1 = TSOP312.., 314.. [package=THT]
  RHT1 = Humidity and Temperature Sensor RHT03

nets:
  N1: Raspberry_Pi1.GPIO4, RHT1.Data-signal
  N2: Raspberry_Pi1.GPIO18, LED2.anode
  N3: Raspberry_Pi1.GPIO15, LED1.anode
  N4: Raspberry_Pi1.GPIO14, IR1.Data
  GND: Raspberry_Pi1.GND, LED1.cathode, LED2.cathode, IR1.GND, RHT1.GND_1
  5V: Raspberry_Pi1.5V, IR1.Vs, RHT1.Vcc

notes:
  Made By:- Sukarna jana
  Switch1 Switch2
  | |
  V V
  <- IR sensor
  DHT11 Temp. & Humi. Sensor
  |
  V
  LCD 16x2 I2C
